# Fritzing sketch schematic (saved by Fritzing 0.9.4)
breadboards: 3

parts:
  Part1 = LCD1602-I2C
  Part2 = RFID-RC522-v2
  L1 = Solenoid
  LED2 = smd LED [color="Green (555nm)" package="0805 [SMD]"]
  LED3 = smd LED [color="Blue (470nm)" package="0805 [SMD]"]
  KY-1 = Keyes Relay [package=THT]
  S4 = Pushbutton [package="[THT]"]
  S5 = Pushbutton [package="[THT]"]
  S6 = Pushbutton [package="[THT]"]
  S7 = Pushbutton [package="[THT]"]
  Part3 = Arduino Nano (Rev3.0) (ICSP)
  LED1 = smd LED [color="Red (633nm)" package="0805 [SMD]"]
  J1 = Power Jack [package=power_jack_slot]
  D1 = Rectifier Diode [part_number=1N4001 package="Melf DO-213 AB [SMD]"]
  J2 = Power Jack [package=power_jack_slot]

nets:
  GND: Part1.GND, Part2.GND, LED2.cathode, LED3.cathode, KY-1.ground, S4.Pin_3, S4.Pin_4, S5.Pin_3, S5.Pin_4, S6.Pin_3, S6.Pin_4, S7.Pin_3, S7.Pin_4, Part3.GND, LED1.cathode, J2.GND
  VCC: Part1.VCC, KY-1.power, Part3.5V
  N1: Part1.SDA, Part3.A4
  N2: Part1.SCL, Part3.A5
  N3: Part2.SDA, Part3.D13/SCK
  N4: Part2.SCK, Part3.D10
  N5: Part2.MOSI, Part3.D11/MOSI
  N6: Part2.MISO, Part3.D12/MISO
  N7: Part2.RST, Part3.D9
  3.3V: Part2.3.3V, Part3.3V3
  N8: L1.pin1, KY-1.NC
  N9: LED2.anode, Part3.D6
  N10: LED3.anode, Part3.D5
  N11: KY-1.signal, Part3.D3
  N12: KY-1.C, J1.GND
  N13: S4.Pin_1, S4.Pin_2, S7.Pin_1, S7.Pin_2, Part3.RESET, Part3.D2
  N14: S5.Pin_1, S5.Pin_2, Part3.A0
  N15: S6.Pin_1, S6.Pin_2, Part3.A1
  N16: Part3.D7, LED1.anode
  N17: Part3.VIN, J2.PWR
  N18: J1.PWR, D1.anode

notes:
  12 V Power Supply
  BTN
  ERASE
  BTN
  RESET
  BTN
  DOOR

custom parts:
  LCD1602-I2C: A standard character display, usually with 2x16 characters. Comes in many colors with LCM1602 IIC attached.
  RFID-RC522-v2: A simple China made RFID-RC522 Reader; do check the pin labels, as this is a MFRC522 based clone.
  Keyes Relay: The Keyes 5V relay module is suitable for SCM development, home appliance control. It uses a 5V~12V TIL control signal which can control DC / AC signal.
